# Fritzing sketch 3 bit counter circuit (saved by Fritzing 0.9.3b)
breadboards: 1

parts:
  Raspberry_Pi_1 = Raspberry Pi 3 [part_number=RPI-3-V1.2]
  S1 = Pushbutton [package="[SMD]"]
  S2 = Pushbutton [package="[SMD]"]
  R1 = Resistor [tolerance=±5% resistance=220 package="0603 [SMD]"]
  R2 = Resistor [tolerance=±5% resistance=220 package="0603 [SMD]"]
  LED2 = LED - 5mm [color="Blue (505nm)" package="5 mm [THT]"]
  LED3 = LED - 5mm [color="Blue (505nm)" package="5 mm [THT]"]
  LED4 = LED - 5mm [color="Blue (505nm)" package="5 mm [THT]"]

nets:
  N1: Raspberry_Pi_1.GPIO2, S2.Pin_3, S2.Pin_4
  N2: Raspberry_Pi_1.GPIO3, S1.Pin_3, S1.Pin_4
  N3: Raspberry_Pi_1.GND, R1.Pin_1, R2.Pin_1, LED2.anode, LED3.anode, LED4.anode
  N4: Raspberry_Pi_1.GPIO21, LED2.cathode
  N5: Raspberry_Pi_1.GPIO20, LED3.cathode
  N6: Raspberry_Pi_1.GPIO16, LED4.cathode
  N7: S1.Pin_1, S1.Pin_2, R2.Pin_0
  N8: S2.Pin_1, S2.Pin_2, R1.Pin_0
