# Fritzing sketch RTC Pi circuit (saved by Fritzing 0.9.3b)
breadboards: 1

parts:
  Raspberry_Pi_1 = Raspberry Pi 3 [part_number=RPI-3-V1.2]
  RTC2 = DIP - 8 pins [chip_label=RTC package="DIP (Dual Inline) [THT]"]

nets:
  N1: Raspberry_Pi_1.3v3, RTC2.pin8
  N2: Raspberry_Pi_1.GND, RTC2.pin4

custom parts:
  DIP - 8 pins: A DIP stand-in part for whatever IC you want. With 8 pins on a 300mil dual inline package (DIP) footprint.
