// Logisim project prac_5_ARNJAM004_WLFJAD001.circ as structural Verilog: 4 circuits, main circuit ALU
module ALU (
  input  A0,
  input  A1,
  input  B0,
  input  B1,
  input  F0,
  input  F1,
  input  F2,
  output Out_LSB,
  output Out_MSB
);

  wire Adder_Subractor_out_lsb, Adder_Subractor_out_msb, Bitwise_AND_OR_out_lsb, Bitwise_AND_OR_out_msb,
       multiplexer_1_out, multiplexer_2_out, Multiply_Divide_by_2_out_lsb, Multiply_Divide_by_2_out_msb;

  Bitwise_AND_OR Bitwise_AND_OR (
    .A0(A0), .B0(B0), .A1(A1), .B1(B1), .F0(F0), .Out_LSB(Bitwise_AND_OR_out_lsb),
    .Out_MSB(Bitwise_AND_OR_out_msb));
  Multiply_Divide_by_2 Multiply_Divide_by_2 (
    .A1(A1), .A0(A0), .Out_LSB(Multiply_Divide_by_2_out_lsb), .Out_MSB(Multiply_Divide_by_2_out_msb), .F0(F0));
  Adder_Incrementer Adder_Subractor (
    .A0(A0), .B0(B0), .F0(F0), .A1(A1), .B1(B1), .Out_LSB(Adder_Subractor_out_lsb),
    .Out_MSB(Adder_Subractor_out_msb), .F1(F1));
  Multiplexer #(.enable("false")) multiplexer_1 (
    .in0(Multiply_Divide_by_2_out_lsb), .in1(Bitwise_AND_OR_out_lsb), .out(multiplexer_1_out), .sel(F1));
  Multiplexer #(.enable("false")) multiplexer_2 (
    .in0(Multiply_Divide_by_2_out_msb), .in1(Bitwise_AND_OR_out_msb), .out(multiplexer_2_out), .sel(F1));
  Multiplexer #(.enable("false")) multiplexer_3 (
    .in0(Adder_Subractor_out_lsb), .in1(multiplexer_1_out), .out(Out_LSB), .sel(F2));
  Multiplexer #(.enable("false")) multiplexer_4 (
    .in0(Adder_Subractor_out_msb), .in1(multiplexer_2_out), .out(Out_MSB), .sel(F2));
endmodule

module Adder_Incrementer (
  input  A0,
  input  B0,
  input  F0,
  input  A1,
  input  B1,
  input  F1,
  output Out_LSB,
  output Out_MSB
);

  wire adder_1_cout, adder_1_out, adder_2_out, multiplexer_1_out, multiplexer_2_out, not_1_out, not_2_out,
       xnor_1_out, xor_1_out, xor_2_out, xor_3_out;

  xor xor_1 (xor_1_out, B0, F0);
  xor xor_2 (xor_2_out, B1, F0);
  xor xor_3 (xor_3_out, A0, A1);
  not not_1 (not_1_out, A0);
  not not_2 (not_2_out, A0);
  xnor xnor_1 (xnor_1_out, A0, A1);
  Adder #(.width(1)) adder_1 (.a(xor_1_out), .b(A0), .out(adder_1_out), .cin(F0), .cout(adder_1_cout));
  Adder #(.width(1)) adder_2 (.a(xor_2_out), .b(A1), .out(adder_2_out), .cin(adder_1_cout));  // open: cout
  Multiplexer #(.enable("false")) multiplexer_1 (.in0(xor_3_out), .in1(xnor_1_out), .out(multiplexer_1_out), .sel(F0));
  Multiplexer #(.enable("false")) multiplexer_2 (.in0(not_1_out), .in1(not_2_out), .out(multiplexer_2_out), .sel(F0));
  Multiplexer #(.enable("false")) multiplexer_3 (.in0(adder_1_out), .in1(multiplexer_2_out), .out(Out_LSB), .sel(F1));
  Multiplexer #(.enable("false")) multiplexer_4 (.in0(adder_2_out), .in1(multiplexer_1_out), .out(Out_MSB), .sel(F1));
endmodule

module Bitwise_AND_OR (
  input  F0,
  input  A0,
  input  B0,
  input  A1,
  input  B1,
  output Out_LSB,
  output Out_MSB
);

  wire and_1_out, and_2_out, or_1_out, or_2_out;

  and and_1 (and_1_out, B0, A0);
  or or_1 (or_1_out, B0, A0);
  and and_2 (and_2_out, B1, A1);
  or or_2 (or_2_out, B1, A1);
  Multiplexer #(.enable("false")) multiplexer_1 (.in0(and_1_out), .in1(or_1_out), .out(Out_LSB), .sel(F0));
  Multiplexer #(.enable("false")) multiplexer_2 (.in0(and_2_out), .in1(or_2_out), .out(Out_MSB), .sel(F0));
endmodule

module Multiply_Divide_by_2 (
  input  F0,
  input  A1,
  input  A0,
  output Out_LSB,
  output Out_MSB
);

  wire multiplexer_1_out, multiplexer_2_out, multiplexer_3_out, multiplexer_4_out;

  Multiplexer #(.enable("false")) multiplexer_1 (.in0(A1), .in1(A0), .out(multiplexer_1_out), .sel(1'b1));
  Multiplexer #(.enable("false")) multiplexer_2 (.in0(A0), .in1(1'b0), .out(multiplexer_2_out), .sel(1'b1));
  Multiplexer #(.enable("false")) multiplexer_3 (.in0(A1), .in1(1'b0), .out(multiplexer_3_out), .sel(1'b1));
  Multiplexer #(.enable("false")) multiplexer_4 (.in0(A0), .in1(A1), .out(multiplexer_4_out), .sel(1'b1));
  Multiplexer #(.enable("false")) multiplexer_5 (
    .in0(multiplexer_2_out), .in1(multiplexer_4_out), .out(Out_LSB), .sel(F0));
  Multiplexer #(.enable("false")) multiplexer_6 (
    .in0(multiplexer_1_out), .in1(multiplexer_3_out), .out(Out_MSB), .sel(F0));
endmodule
